# Fritzing sketch Display_Board (saved by Fritzing 0.9.3b)
breadboards: 1

parts:
  LCD1 = LCD screen
  U1 = mystery part, 4 pins [chip_label="I²C Controller"]
  U2 = mystery part, 16 pins [chip_label=?]
  J1 = double row female pin header, 2 pins [form="♀ (female)"]
  J2 = double row male pin header, 2 pins [form="♂ (male)"]

nets:
  N1: LCD1.VSS, U2.pin16
  N2: LCD1.VDD, U2.pin15
  N3: LCD1.V0, U2.pin14
  N4: LCD1.RS, U2.pin13
  N5: LCD1.R/W, U2.pin12
  N6: LCD1.E, U2.pin11
  N7: LCD1.DB0, U2.pin10
  N8: LCD1.DB1, U2.pin9
  N9: LCD1.DB2, U2.pin8
  N10: LCD1.DB3, U2.pin7
  N11: LCD1.DB4, U2.pin6
  N12: LCD1.DB5, U2.pin5
  N13: LCD1.DB6, U2.pin4
  N14: LCD1.DB7, U2.pin3
  N15: LCD1.LED+, U2.pin2
  N16: LCD1.LED-, U2.pin1
  N17: U1.pin1, J2.pin2
  N18: U1.pin2, J2.pin1
  N19: U1.pin3, J1.pin2
  N20: U1.pin4, J1.pin1

notes:
  Super Nova Pinball, Display Board  Part of  github.com/racer0815/supernova_pinball 
