# Fritzing sketch Main_Circuit_Board (saved by Fritzing 0.9.3b)
breadboards: 1

parts:
  Bauteil1 = Arduino Uno (Rev3)
  U1 = Voltage Regulator - 5V [package="TO220 [THT]"]
  J1 = Screw terminal - 2 pins [package=THT]
  U5 = 74HC595 [package="DIP16 [THT]"]
  J2 = double row female pin header, 8 pins [form="♀ (female)"]
  J3 = double row female pin header, 8 pins [form="♀ (female)"]
  U6 = 74HC595 [package="DIP16 [THT]"]
  J4 = double row female pin header, 8 pins [form="♀ (female)"]
  J5 = double row female pin header, 8 pins [form="♀ (female)"]
  U7 = 74HC595 [package="DIP16 [THT]"]
  J6 = double row female pin header, 8 pins [form="♀ (female)"]
  J7 = double row female pin header, 8 pins [form="♀ (female)"]
  J8 = shrouded pin header, 6 pins [form="♂ (shrouded male)"]
  LED1 = LED - 5mm [color="Red (633nm)" package="5 mm [THT]"]
  LED2 = LED - 5mm [color="Yellow (574nm)" package="5 mm [THT]"]
  R1 = Resistor [tolerance=±5% resistance=220 package=THT]
  R2 = Resistor [tolerance=±5% resistance=220 package=THT]
  J9 = shrouded pin header, 6 pins [form="♂ (shrouded male)"]
  J10 = shrouded pin header, 6 pins [form="♂ (shrouded male)"]

nets:
  N1: Bauteil1.A0, J8.pin6
  N2: Bauteil1.A1, J8.pin5
  N3: Bauteil1.A2, J8.pin4
  N4: Bauteil1.A3, J8.pin3
  GND: Bauteil1.GND, U1.GND, J1.pin1, U5.GND, U5.OE, J3.pin1, J3.pin2, J3.pin3, J3.pin4, J3.pin5, J3.pin6, J3.pin7, J3.pin8, U6.GND, U6.OE, J5.pin1, J5.pin2, J5.pin3, J5.pin4, J5.pin5, J5.pin6, J5.pin7, J5.pin8, U7.GND, U7.OE, J7.pin1, J7.pin2, J7.pin3, J7.pin4, J7.pin5, J7.pin6, J7.pin7, J7.pin8, LED1.cathode, LED2.cathode, J10.pin1, J10.pin2, J10.pin3, J10.pin4, J10.pin5, J10.pin6
  N5: Bauteil1.A4/SDA, J8.pin2
  N6: Bauteil1.A5/SCL, J8.pin1
  N7: Bauteil1.D3_PWM, R1.Pin_0
  N8: Bauteil1.D4, U7.DS
  N9: Bauteil1.D5_PWM, U5.ST_CP, U6.ST_CP, U7.ST_CP
  N10: Bauteil1.D6_PWM, U5.SH_CP, U6.SH_CP, U7.SH_CP
  VCC: Bauteil1.VIN, U1.output_voltage, U5.MR, U5.VCC, U6.MR, U6.VCC, U7.MR, U7.VCC, R2.Pin_0, J9.pin1, J9.pin2, J9.pin3, J9.pin4, J9.pin5, J9.pin6
  N11: U1.input_voltage, J1.pin2
  N12: U5.Q1, J2.pin8
  N13: U5.Q2, J2.pin7
  N14: U5.Q3, J2.pin6
  N15: U5.Q4, J2.pin5
  N16: U5.Q5, J2.pin4
  N17: U5.Q6, J2.pin3
  N18: U5.Q7, J2.pin2
  N19: U5.DS, U6.Q7'
  N20: U5.Q0, J2.pin1
  N21: U6.Q1, J4.pin8
  N22: U6.Q2, J4.pin7
  N23: U6.Q3, J4.pin6
  N24: U6.Q4, J4.pin5
  N25: U6.Q5, J4.pin4
  N26: U6.Q6, J4.pin3
  N27: U6.Q7, J4.pin2
  N28: U6.DS, U7.Q7'
  N29: U6.Q0, J4.pin1
  N30: U7.Q1, J6.pin8
  N31: U7.Q2, J6.pin7
  N32: U7.Q3, J6.pin6
  N33: U7.Q4, J6.pin5
  N34: U7.Q5, J6.pin4
  N35: U7.Q6, J6.pin3
  N36: U7.Q7, J6.pin2
  N37: U7.Q0, J6.pin1
  N38: LED1.anode, R1.Pin_1
  N39: LED2.anode, R2.Pin_1

notes:
  Super Nova Pinball, Main Circuit Board
