# Fritzing sketch Motordriver (saved by Fritzing 0.9.3b)
breadboards: 1

parts:
  J1 = Screw terminal - 2 pins [package=THT]
  U1 = Voltage Regulator - 5V [package="TO220 [THT]"]
  Q1 = NPN-Transistor [package="TO92 [THT]"]
  J2 = male pin header, 1 pin [form="♂ (male)"]
  J3 = male pin header, 1 pin [form="♂ (male)"]
  J4 = female pin header, 1 pin [form="♀ (female)"]

nets:
  N1: J1.pin1, U1.GND, J4.pin1
  N2: J1.pin2, U1.input_voltage
  N3: U1.output_voltage, Q1.C
  N4: Q1.E, J3.pin1
  N5: Q1.B, J2.pin1

notes:
  Super Nova Pinball, Motordriver  Part of  github.com/racer0815/supernova_pinball 
