# Fritzing sketch Sensor_Controller (saved by Fritzing 0.9.3b)
breadboards: 1

parts:
  R1 = Resistor [tolerance=±5% resistance=10k package=THT]
  R2 = Resistor [tolerance=±5% resistance=10k package=THT]
  R3 = Resistor [tolerance=±5% resistance=10k package=THT]
  R4 = Resistor [tolerance=±5% resistance=10k package=THT]
  J2 = double row female pin header, 4 pins [form="♀ (female)"]
  J1 = double row male pin header, 4 pins [form="♂ (male)"]
  J3 = male pin header, 1 pin [form="♂ (male)"]

nets:
  N1: R1.Pin_0, R2.Pin_0, R3.Pin_0, R4.Pin_0, J3.pin1
  N2: R1.Pin_1, J2.pin1, J1.pin1
  N3: R2.Pin_1, J2.pin4, J1.pin4
  N4: R3.Pin_1, J2.pin3, J1.pin3
  N5: R4.Pin_1, J2.pin2, J1.pin2

notes:
  Super Nova Pinball, Sensor Controller  Part of  github.com/racer0815/supernova_pinball 
  Sensorport to Main Circuit Board
  GND
  Sensor Input
